# Fritzing sketch inteligent_room (saved by Fritzing 0.7.11b)
breadboards: 1

parts:
  Arduino1 = Arduino
  T1 = TMP36 Temperature Sensor [thermistor_type=NTC package="TO92 [THT]"]
  LED1 = LED - 5mm [color="Red (633nm)" package="5 mm [THT]"]
  R1 = Photocell (LDR) [package=THT]
  LED2 = LED - 5mm [color="Red (633nm)" package="5 mm [THT]"]
  R2 = Resistor [tolerance=±5% resistance=220 package=THT]
  R3 = Resistor [tolerance=±5% resistance=220 package=THT]
  R4 = Resistor [tolerance=±5% resistance=10k package=THT]
  R5 = Resistor [tolerance=±5% resistance=10k package=THT]

nets:
  GND: Arduino1.GND, T1.GND, LED1.anode, LED2.anode, R5.Pin_1
  N1: Arduino1.D5, R2.Pin_0
  N2: Arduino1.D3, R3.Pin_1
  N3: Arduino1.+5V, T1.+Vs, R1.pin_0
  N4: Arduino1.A0, R1.pin_1, R4.Pin_0
  N5: Arduino1.A5, T1.Vout
  N6: LED1.cathode, R2.Pin_1
  N7: LED2.cathode, R3.Pin_0
  N8: R4.Pin_1, R5.Pin_0

notes:
  temperature sensor
  Lamp1, photoresistor and Lamp0("SUN")
